// Logisim project ZalSap2AJourney2.circ as structural Verilog: 1 circuit, main circuit main
module main (
  input  in_1,
  input  Run,
  output Program_Counter_Load_Enable,
  output [7:0] ALU_Output,
  output [3:0] Bus_Output,
  output [7:0] Output,
  output T3,
  output T6,
  output [5:0] T_State
);

  wire and_1_out, clock_1_out, nand_1_out, not_1_out, not_2_out, not_3_out, not_4_out, not_5_out, not_6_out,
       not_7_out, not_8_out, not_9_out, not_10_out, not_11_out, not_12_out, not_13_out, or_1_out, or_2_out;
  wire [3:0] counter_1_q, ram_1_data, register_1_q;
  wire [7:0] adder_1_out, counter_2_q, multiplexer_1_out, register_2_q, register_4_q, rom_1_data, xor_1_out;
  wire [15:0] rom_2_data;

  or or_1 (or_1_out, Program_Counter_Load_Enable, rom_2_data[13]);
  not not_1 (not_1_out, Run);
  and and_1 (and_1_out, clock_1_out, Run, nand_1_out);
  not not_2 (not_2_out, and_1_out);
  Register #(.width(4)) register_1 (.D(Bus_Output), .en(not_3_out), .Q(register_1_q), .clk(and_1_out));  // open: clr
  not not_3 (not_3_out, rom_2_data[9]);
  Counter #(.width(4), .max('hf)) counter_1 (
    .load(or_1_out), .D(Bus_Output), .count(rom_2_data[11]), .Q(counter_1_q), .clk(not_2_out), .clr(not_1_out));  // open: carry
  assign Bus_Output = rom_2_data[10] ? counter_1_q : 4'bz;  // Controlled_Buffer controlled_buffer_1
  not not_4 (not_4_out, rom_2_data[8]);
  Clock clock_1 (.out(clock_1_out));
  not not_5 (not_5_out, rom_2_data[12]);
  not not_6 (not_6_out, and_1_out);
  RAM #(.addrWidth(4), .bus("asynch")) ram_1 (
    .addr(register_1_q), .data({ram_1_data, Bus_Output}), .sel(not_4_out), .ld(not_5_out), .clr(in_1));
  Register register_2 (
    .D({ram_1_data, Bus_Output}), .en(not_7_out), .Q(register_2_q), .clk(and_1_out), .clr(not_1_out));
  not not_7 (not_7_out, rom_2_data[7]);
  D_Flip_Flop d_ff_1 (.clk(not_6_out), .D(T6), .Q(T_State[5]), .preset(not_1_out));  // open: Qn, en, reset
  or or_2 (or_2_out, T3, T6);
  D_Flip_Flop d_ff_2 (.clk(not_6_out), .D(T_State[5]), .Q(T_State[4]), .reset(not_1_out));  // open: Qn, preset, en
  Hex_Digit_Display hex_digit_display_1 (.value(rom_2_data[15:12]));  // open: dp
  assign Bus_Output = not_8_out ? register_2_q[3:0] : 4'bz;  // Controlled_Buffer controlled_buffer_2
  not not_8 (not_8_out, rom_2_data[6]);
  nand nand_1 (nand_1_out, register_2_q[7], register_2_q[6], register_2_q[5], register_2_q[4]);
  ROM #(.addrWidth(4)) rom_1 (.addr(register_2_q[7:4]), .data(rom_1_data));  // open: sel
  Multiplexer #(.select(2), .width(8), .enable("false")) multiplexer_1 (
    .in1({8{1'b0}}), .in2(rom_1_data), .out(multiplexer_1_out), .sel({T3, T6}));  // open: in0, in3
  Counter #(.trigger("falling")) counter_2 (
    .load(or_2_out), .D(multiplexer_1_out), .count(not_9_out), .Q(counter_2_q), .clk(and_1_out),
    .clr(not_1_out));  // open: carry
  not not_9 (not_9_out, or_2_out);
  D_Flip_Flop d_ff_3 (.clk(not_6_out), .D(T_State[4]), .Q(T3), .reset(not_1_out));  // open: Qn, preset, en
  Hex_Digit_Display hex_digit_display_2 (.value(rom_2_data[11:8]));  // open: dp
  Hex_Digit_Display hex_digit_display_3 (.value(rom_2_data[7:4]));  // open: dp
  D_Flip_Flop d_ff_4 (.clk(not_6_out), .D(T3), .Q(T_State[2]), .reset(not_1_out));  // open: Qn, preset, en
  Hex_Digit_Display hex_digit_display_4 (.value(rom_2_data[3:0]));  // open: dp
  ROM #(.dataWidth(16)) rom_2 (.addr(counter_2_q), .data(rom_2_data));  // open: sel
  D_Flip_Flop d_ff_5 (.clk(not_6_out), .D(T_State[2]), .Q(T_State[1]), .reset(not_1_out));  // open: Qn, preset, en
  D_Flip_Flop d_ff_6 (.clk(not_6_out), .D(T_State[1]), .Q(T6), .reset(not_1_out));  // open: Qn, preset, en
  not not_10 (not_10_out, rom_2_data[5]);
  Hex_Digit_Display hex_digit_display_5 (.value(Output[7:4]));  // open: dp
  Hex_Digit_Display hex_digit_display_6 (.value(Output[3:0]));  // open: dp
  Register register_3 (.D({ram_1_data, Bus_Output}), .en(not_10_out), .Q(ALU_Output), .clk(and_1_out));  // open: clr
  Register register_4 (.D({ram_1_data, Bus_Output}), .en(not_11_out), .Q(register_4_q), .clk(and_1_out));  // open: clr
  not not_11 (not_11_out, rom_2_data[1]);
  assign {ram_1_data, Bus_Output} = rom_2_data[4] ? ALU_Output : 8'bz;  // Controlled_Buffer controlled_buffer_3
  assign xor_1_out = register_4_q ^ {8{rom_2_data[3]}};  // XOR_Gate xor_1, 8 bits wide
  Register register_5 (.D({ram_1_data, Bus_Output}), .en(not_12_out), .Q(Output), .clk(and_1_out));  // open: clr
  not not_12 (not_12_out, rom_2_data[0]);
  nor nor_1 (Program_Counter_Load_Enable, ALU_Output[0], ALU_Output[1], ALU_Output[2], ALU_Output[3], ALU_Output[4], ALU_Output[5], ALU_Output[6], ALU_Output[7], not_13_out);
  not not_13 (not_13_out, rom_2_data[14]);
  assign {ram_1_data, Bus_Output} = rom_2_data[2] ? adder_1_out : 8'bz;  // Controlled_Buffer controlled_buffer_4
  Adder adder_1 (.a(xor_1_out), .b(ALU_Output), .out(adder_1_out), .cin(rom_2_data[3]));  // open: cout

  assign {T_State[3], T_State[0]} = {T3, T6};

  // Notes on the sheet:
  //   PC
  //   MAR
  //   Instruction Register
  //   Controller/sequencer
  //   Address ROM
  //   T-State Sequencer
  //   contents of rom_1 (hex, n*v repeats v):
  //   3 6 9 f 12 15 18 7*0 c
  //   Control ROM
  //   contents of rom_2 (hex, n*v repeats v):
  //   5e3 be3 263 1a3 2c3 3e3 1a3 2e1 3c7 1a3 2e1 3cf 3f2 3e3 3e3 1a3 12f3 3e3 23a3 3e3 3e3 43a3 3e3 3e3
  //   1a3 e3 2c3
  //   Bus Input
  //   Temporary Script
  //   08 19 3a e0
  //   f0 00 00 00
  //   12 13 00 00
  //   A Register
  //   Adder/Subtracter
  //   B Register
  //   Output Register
endmodule
